# Fritzing sketch VisualSketch (saved by Fritzing 0.9.2b)
breadboards: 1

parts:
  Part1 = Arduino Mega 2560 (Rev3)
  Q1 = TRANSISTOR_NPN [part_number=TIP31 package=to-92-ammo]
  D1 = Rectifier Diode [part_number=1N4001 package="300 mil [THT]"]
  M1 = DC Motor [part_number="12V 0.44A FAN"]
  M2 = DC Motor [part_number="12V 0.44A FAN"]
  M3 = DC Motor
  R1 = Resistor [tolerance=±5% resistance=1k package="0805 [SMD]"]
  R2 = Resistor [tolerance=±5% resistance=10k package="2010 [SMD]"]
  R3 = Temperature Sensor (Thermistor) [thermistor_type=NTC package=THT]

nets:
  N1: Part1.A0, R2.Pin_1, R3.pin_0
  N2: Part1.D9_PWM, R1.Pin_1
  N3: Part1.5V, R2.Pin_0
  N4: Part1.GND, Q1.B, D1.anode, M1.pin_1, M2.pin_1, M3.pin_1, R3.pin_1
  N5: Q1.C, R1.Pin_0
  N6: D1.cathode, M1.pin_2, M2.pin_2, M3.pin_2

notes:
  +12V power supply
  Power supply ground
