# Fritzing sketch Circuit_diagram_thermistors (saved by Fritzing 0.9.2b)
breadboards: 1

parts:
  R3 = Resistor [tolerance=±5% resistance=10k package="0603 [SMD]"]
  R4 = Resistor [tolerance=±5% resistance=10k package="0603 [SMD]"]
  R5 = Resistor [tolerance=±5% resistance=10k package="0603 [SMD]"]
  Part1 = Arduino Mega 2560 (Rev3)
  JP8 = Header 10 [package=1x10-2mm-smd]
  JP9 = Header 10 [package=1x10-2mm-smd]  # not connected

nets:
  N1: R3.Pin_0, Part1.A1, JP8.6
  N2: R3.Pin_1, R4.Pin_1, R5.Pin_1
  N3: R4.Pin_0, Part1.A0, JP8.5
  N4: R5.Pin_0, Part1.A2, JP8.7

notes:
  There are three thermistors on the telescope: ambient, primary, secondary temperatures.
  The 10k resistors are for voltage dividers
  Arduino pinout:
  Ambient - A0
  Primary - A1
  Secondary - A2
  20-pin array:
  Ambient - pin5
  Primary - pin6
  Secondary - pin7
