# Fritzing sketch fans_diagram (saved by Fritzing 0.9.2b)
breadboards: 1

parts:
  Part1 = Arduino Mega 2560 (Rev3)
  Q2 = Basic FET N-Channel [part_number=IRF540N package="TO220 [THT]"]
  D1 = Rectifier Diode [part_number=1N4001 package="300 mil [THT]"]
  R1 = Resistor [tolerance=±5% resistance=10k package="0603 [SMD]"]
  R2 = Resistor [tolerance=±5% resistance=1k package="0603 [SMD]"]
  JP1 = Header 10 [package=1x10-2mm-smd]  # not connected
  JP2 = Header 10 [package=1x10-2mm-smd]
  V1 = DC Power [voltage=5]  # not connected
  JP3 = Header 10 [package=1x10-2mm-smd]  # not connected
  JP4 = Header 10 [package=1x10-2mm-smd]  # not connected

nets:
  N1: Part1.D9_PWM, R2.Pin_0
  N2: Part1.GND, Q2.source, D1.anode, R1.Pin_0
  N3: Q2.gate, R1.Pin_1, R2.Pin_1
  N4: Q2.drain, D1.cathode, JP2.8

notes:
  fans: Pin 8 on array that connects to telescope (fans are not shown in this schematic)
  11 12 13 14 15 16 17 18 19 20
  1 2 3 4 5 6 7 8 9 10
