# Fritzing sketch heater_diagram (saved by Fritzing 0.9.2b)
breadboards: 1

parts:
  Part2 = Arduino Mega 2560 (Rev3)
  Q3 = Basic FET N-Channel [part_number=IRF540N package="TO220 [THT]"]
  D2 = Rectifier Diode [part_number=1N4001 package="300 mil [THT]"]
  JP5 = Header 10 [package=1x10-2mm-smd]  # not connected
  JP6 = Header 10 [package=1x10-2mm-smd]  # not connected
  JP7 = Header 10 [package=1x10-2mm-smd]
  JP8 = Header 10 [package=1x10-2mm-smd]  # not connected
  R3 = Resistor [tolerance=±5% resistance=10k package="0603 [SMD]"]
  R4 = Resistor [tolerance=±5% resistance=1k package="0603 [SMD]"]

nets:
  N1: Part2.D12_PWM, R4.Pin_0
  N2: Part2.GND, Q3.source, D2.anode, R3.Pin_0
  N3: Q3.gate, R3.Pin_1, R4.Pin_1
  N4: Q3.drain, D2.cathode, JP7.9

notes:
  fans: Pin 9 on array that connects to telescope heater (heater not shown in this schematic)
  11 12 13 14 15 16 17 18 19 20
  1 2 3 4 5 6 7 8 9 10
