# Fritzing sketch motor_diagram (saved by Fritzing 0.9.2b)
breadboards: 1

parts:
  Part1 = Arduino Mega 2560 (Rev3)
  12V_power_supply = Power Jack [package=power_jack_pth]
  JP5 = Header 10 [package=1x10-2mm-smd]
  JP6 = Header 10 [package=1x10-2mm-smd]
  U2 = IC, DIP package, 8 pins [chip_label=IC part_number=LS7184N]
  U3 = IC, DIP package, 20 pins [chip_label=IC part_number=MC33887APVW]
  R1 = Resistor [tolerance=±5% resistance=330k part_number=360K package="2512 [SMD]"]

nets:
  N1: Part1.D21/SCL, U2.pin7
  N2: Part1.D20/SDA, U2.pin8
  N3: Part1.D10_PWM, U3.pin11
  N4: Part1.GND, U3.pin14, U3.pin19, U3.pin20
  N5: Part1.D2_PWM, U3.pin12
  N6: Part1.D3_PWM, U3.pin8
  N7: Part1.D4_PWM, U3.pin13
  N8: Part1.D5_PWM, U3.pin18
  N9: Part1.D49, JP5.3, U2.pin4
  N10: 12V_power_supply.GNDBREAK, U2.pin3, U3.pin1, U3.pin2, U3.pin10, R1.Pin_1
  N11: 12V_power_supply.PWR, U2.pin2, U3.pin6, U3.pin7, U3.pin15
  N12: JP5.1, U3.pin16
  N13: JP6.1, U3.pin5
  N14: JP6.3, U2.pin5
  N15: U2.pin1, R1.Pin_0

notes:
  11 12 13 14 15 16 17 18 19 20
  20 PIN ARRAY
  1 2 3 4 5 6 7 8 9 10
